# Fritzing sketch uno_r4_opamp (saved by Fritzing 0.9.3b)
breadboards: 1

parts:
  A1 = Arduino R4 Minima
  C1 = Ceramic Capacitor [capacitance=100nF package="100 mil [THT, multilayer]"]
  R1 = Resistor [tolerance=±5% resistance=100 package=THT]
  Q1 = Basic FET N-Channel [part_number=STP60N package="TO220 [THT]"]
  R2 = Resistor [tolerance=±5% resistance=4.7 package=THT]
  R3 = Resistor [tolerance=±5% resistance=2k package=THT]
  C2 = Ceramic Capacitor [capacitance=1nF package="100 mil [THT, multilayer]"]
  J1 = female pin header, 2 pins [form="♀ (female)"]

nets:
  N1: A1.Pin_6, C1.0, R2.Pin_1, J1.pin2
  N2: A1.Pin_9, A1.Pin_10
  N3: A1.Pin_11, R3.Pin_0, C2.0
  N4: A1.Pin_12, R1.Pin_0, C2.1
  N5: A1.Pin_14, Q1.source, R2.Pin_0, R3.Pin_1
  N6: R1.Pin_1, Q1.gate
  N7: Q1.drain, J1.pin1

notes:
  ADC
  100 nF
  1 nF
  Battery
  +

custom parts:
  Arduino R4 Minima: Introducing the Arduino UNO R4 Minima! This board boasts the RA4M1 microprocessor from Renesas, delivering increased processing power, expanded memory, and additional peripherals.
